// Logisim project jcpu.circ as structural Verilog: 7 circuits, main circuit main
module main (
);

  alu alu_1 ();  // open: c_in, a_in, b_in, op_in, data_out
  pc pc_1 ();  // open: data_in, w_in, s_in, clk_in, data_out
endmodule

module alu (
  input  c_in,
  input  [3:0] a_in,
  input  [3:0] b_in,
  input  [3:0] op_in,
  output [3:0] data_out
);

  wire [3:0] demultiplexer_1_out0, demultiplexer_2_out0;

  Demultiplexer #(.select(4), .width(4)) demultiplexer_1 (
    .out0(demultiplexer_1_out0), .in(a_in), .sel(op_in));  // open: out1, out2, out3, out4, out5, out6, out7, out8, out9, out10, out11, out12, out13, out14, out15
  Demultiplexer #(.select(4), .width(4)) demultiplexer_2 (
    .out0(demultiplexer_2_out0), .in(b_in), .sel(op_in));  // open: out1, out2, out3, out4, out5, out6, out7, out8, out9, out10, out11, out12, out13, out14, out15
  adder_unit adder_unit_1 (
    .a_in(demultiplexer_1_out0), .b_in(demultiplexer_2_out0), .c_in(c_in), .data_out(data_out));  // open: c_out
endmodule

module pc (
  input  [3:0] data_in,
  input  w_in,
  input  s_in,
  input  clk_in,
  output [3:0] data_out
);

  wire controlled_buffer_1_out;
  wire [3:0] incrementer_unit_1_data_out, multiplexer_1_out;

  assign controlled_buffer_1_out = w_in ? clk_in : 1'bz;  // Controlled_Buffer controlled_buffer_1
  Multiplexer #(.width(4)) multiplexer_1 (
    .in0(incrementer_unit_1_data_out), .in1(data_in), .out(multiplexer_1_out), .sel(s_in));
  D_Flip_Flop d_ff_1 (
    .D(multiplexer_1_out[0]), .clk(controlled_buffer_1_out), .Q(data_out[0]));  // open: Qn, preset, reset
  D_Flip_Flop d_ff_2 (
    .D(multiplexer_1_out[1]), .clk(controlled_buffer_1_out), .Q(data_out[1]));  // open: Qn, preset, reset
  D_Flip_Flop d_ff_3 (
    .D(multiplexer_1_out[2]), .clk(controlled_buffer_1_out), .Q(data_out[2]));  // open: Qn, preset, reset
  D_Flip_Flop d_ff_4 (
    .D(multiplexer_1_out[3]), .clk(controlled_buffer_1_out), .Q(data_out[3]));  // open: Qn, preset, reset
  incrementer_unit incrementer_unit_1 (.a_in(data_out), .data_out(incrementer_unit_1_data_out));  // open: c_out
endmodule

module adder_unit (
  input  [3:0] a_in,
  input  c_in,
  input  [3:0] b_in,
  output [3:0] data_out,
  output c_out
);

  wire and_1_out, and_2_out, and_3_out, and_4_out, and_5_out, and_6_out, and_7_out, and_8_out, or_1_out,
       or_2_out, or_3_out, xor_1_out, xor_2_out, xor_3_out, xor_4_out;

  xor xor_1 (xor_1_out, a_in[0], b_in[0]);
  and and_1 (and_1_out, a_in[0], b_in[0]);
  xor xor_2 (xor_2_out, a_in[1], b_in[1]);
  and and_2 (and_2_out, a_in[1], b_in[1]);
  xor xor_3 (xor_3_out, a_in[2], b_in[2]);
  and and_3 (and_3_out, a_in[2], b_in[2]);
  xor xor_4 (xor_4_out, a_in[3], b_in[3]);
  and and_4 (and_4_out, a_in[3], b_in[3]);
  xor xor_5 (data_out[0], c_in, xor_1_out);
  and and_5 (and_5_out, c_in, xor_1_out);
  xor xor_6 (data_out[1], or_1_out, xor_2_out);
  and and_6 (and_6_out, or_1_out, xor_2_out);
  xor xor_7 (data_out[2], or_2_out, xor_3_out);
  and and_7 (and_7_out, or_2_out, xor_3_out);
  xor xor_8 (data_out[3], or_3_out, xor_4_out);
  and and_8 (and_8_out, or_3_out, xor_4_out);
  or or_1 (or_1_out, and_5_out, and_1_out);
  or or_2 (or_2_out, and_6_out, and_2_out);
  or or_3 (or_3_out, and_7_out, and_3_out);
  or or_4 (c_out, and_8_out, and_4_out);
endmodule

module subtractor_unit (
  input  op_a_in,
  input  op_b_in,
  input  b_in,
  output s_out,
  output b_out
);

  wire and_1_out, not_1_out, xor_1_out;

  buf xor_1 (xor_1_out, op_a_in);  // XOR_Gate
  buf and_1 (and_1_out, not_1_out);  // AND_Gate
  // NOT_Gate not_1 has open pins: in=open, out=not_1_out
endmodule

module incrementer_unit (
  input  [3:0] a_in,
  output [3:0] data_out,
  output c_out
);

  wire and_1_out, and_2_out, and_3_out;

  xor xor_1 (data_out[0], 1'b1, a_in[0]);
  and and_1 (and_1_out, 1'b1, a_in[0]);
  xor xor_2 (data_out[1], and_1_out, a_in[1]);
  and and_2 (and_2_out, and_1_out, a_in[1]);
  xor xor_3 (data_out[2], and_2_out, a_in[2]);
  and and_3 (and_3_out, and_2_out, a_in[2]);
  xor xor_4 (data_out[3], and_3_out, a_in[3]);
  and and_4 (c_out, and_3_out, a_in[3]);
endmodule

module register_unit (
  input  [3:0] data_in,
  input  clk_in,
  output [3:0] data_out
);

  D_Flip_Flop d_ff_1 (.D(data_in[0]), .clk(clk_in));  // open: Q, Qn, preset, reset
  D_Flip_Flop d_ff_2 (.D(data_in[1]), .clk(clk_in));  // open: Q, Qn, preset, reset
  D_Flip_Flop d_ff_3 (.D(data_in[2]), .clk(clk_in));  // open: Q, Qn, preset, reset
  D_Flip_Flop d_ff_4 (.D(data_in[3]), .clk(clk_in));  // open: Q, Qn, preset, reset
endmodule
